# Fritzing sketch temp2iot (saved by Fritzing 0.9.5d)

parts:
  WeMos_D1_Mini1 = WeMos D1 Mini
  DS1 = DS18B20 1-Wire Temperature Sensor [part_number=DS18B20]
  R1 = Resistor [tolerance=±5% resistance=4.7k package=THT]

nets:
  5V: WeMos_D1_Mini1.5V, DS1.VDD, R1.Pin_1
  N1: WeMos_D1_Mini1.D2, DS1.DQ, R1.Pin_0
  N2: WeMos_D1_Mini1.G, DS1.GND
